// Logisim project alu.circ as structural Verilog: 14 circuits, main circuit main
module main (
);


  // Notes on the sheet:
  //   cs31 lab3, part2:alu
  //   Zakir Hossain, Neel Gupta
endmodule

module subtractor (
  input  [7:0] X,
  input  [7:0] Y,
  output [7:0] out_3,
  output out_4
);

  wire [7:0] not_1_out;

  assign not_1_out = ~Y;  // NOT_Gate not_1, 8 bits wide
  Adder_part adder_1 (.a(X), .b(not_1_out), .out(out_3), .cin(1'b1), .cout(out_4));
endmodule

module OR (
  input  [7:0] X,
  input  [7:0] Y,
  output [7:0] out_3
);

  assign out_3 = X | Y;  // OR_Gate or_1, 8 bits wide
endmodule

module AND (
  input  [7:0] X,
  input  [7:0] Y,
  output [7:0] out_3
);

  assign out_3 = X & Y;  // AND_Gate and_1, 8 bits wide
endmodule

module Adder (
  input  [7:0] X,
  input  [7:0] Y,
  output [7:0] out_3,
  output C_out
);

  Adder_part adder_1 (.a(X), .b(Y), .out(out_3), .cout(C_out));  // open: cin
endmodule

module ShiftLeft (
  input  [7:0] X,
  input  [7:0] Y,
  output [7:0] out_3
);

  Shifter shifter_1 (.in(X), .\dist (Y[2:0]), .out(out_3));
endmodule

module LogicalRight (
  input  [7:0] X,
  input  [7:0] Y,
  output [7:0] out_3
);

  Shifter #(.shift("lr")) shifter_1 (.in(X), .\dist (Y[2:0]), .out(out_3));
endmodule

module ArithmeticRight (
  input  [7:0] X,
  input  [7:0] Y,
  output [7:0] out_3
);

  Shifter #(.shift("ar")) shifter_1 (.in(X), .\dist (Y[2:0]), .out(out_3));
endmodule

module LessThan (
  input  [7:0] X,
  input  [7:0] Y,
  output out_3,
  output [7:0] out_4
);

  not not_1 (out_4[7], 1'b1);
  Comparator comparator_1 (.a(X), .b(Y), .eq(out_3), .lt(out_4[0]));  // open: gt

  assign out_4[6:1] = {6{out_4[7]}};
endmodule

module Multiplexor (
  input  [2:0] in_1,
  input  [7:0] in_2,
  input  [7:0] in_3,
  input  [7:0] in_4,
  input  [7:0] in_5,
  input  [7:0] in_6,
  input  [7:0] in_7,
  input  [7:0] in_8,
  input  [7:0] in_9,
  output [7:0] out_10
);

  Multiplexer #(.select(3), .width(8), .enable("false")) multiplexer_1 (
    .in0(in_2), .in1(in_3), .in2(in_4), .in3(in_5), .in4(in_6), .in5(in_7), .in6(in_8), .in7(in_9),
    .out(out_10), .sel(in_1));

  // Notes on the sheet:
  //   Eight 8-bit inputs
endmodule

module AllTogether (
  input  [2:0] op_code,
  input  [7:0] X,
  input  [7:0] Y,
  output [7:0] Result,
  output SF,
  output ZF,
  output CF,
  output OF,
  output EQ
);

  wire Adder_c_out, or_2_out, Subtractor_out_4;
  wire [7:0] Adder_out_3, AND_out_3, Arithmetic_Right_out_3, Less_Than_out_4, Logical_Right_out_3, OR_out_3,
       Shift_Left_out_3, Subtractor_out_3;

  OR OR (.X(X), .Y(Y), .out_3(OR_out_3));
  AND AND (.X(X), .Y(Y), .out_3(AND_out_3));
  Adder Adder (.X(X), .Y(Y), .C_out(Adder_c_out), .out_3(Adder_out_3));
  subtractor Subtractor (.X(X), .Y(Y), .out_4(Subtractor_out_4), .out_3(Subtractor_out_3));
  ShiftLeft Shift_Left (.X(Y), .Y(X), .out_3(Shift_Left_out_3));
  LogicalRight Logical_Right (.X(X), .Y(Y), .out_3(Logical_Right_out_3));
  ArithmeticRight Arithmetic_Right (.X(X), .Y(Y), .out_3(Arithmetic_Right_out_3));
  LessThan Less_Than (.X(X), .Y(Y), .out_3(EQ), .out_4(Less_Than_out_4));
  Multiplexor multiplexor_1 (
    .in_1(op_code), .in_2(OR_out_3), .in_3(AND_out_3), .in_4(Adder_out_3), .in_5(Subtractor_out_3),
    .in_6(Shift_Left_out_3), .in_7(Logical_Right_out_3), .in_8(Arithmetic_Right_out_3),
    .in_9(Less_Than_out_4), .out_10(Result));
  OF of_1 (.op_code(op_code), .X(X), .Y(Y), .Output(Result), .OF(OF));
  CF cf_1 (.op_code(op_code), .Adder(Adder_c_out), .Subtractor(Subtractor_out_4), .out_4(CF));
  or or_2 (or_2_out, Result[0], Result[1], Result[2], Result[3], Result[4], Result[5], Result[6], Result[7]);
  not not_1 (ZF, or_2_out);

  assign SF = Result[7];
endmodule

module OF (
  input  [2:0] op_code,
  input  [7:0] X,
  input  [7:0] Y,
  input  [7:0] Output,
  output OF
);

  wire and_1_out, and_2_out, not_1_out, not_2_out, xor_1_out, xor_2_out, xor_3_out, xor_4_out;

  xor xor_1 (xor_1_out, X[7], Output[7]);
  xor xor_2 (xor_2_out, X[7], Y[7]);
  xor xor_3 (xor_3_out, X[7], Y[7]);
  not not_1 (not_1_out, 1'b1);
  not not_2 (not_2_out, xor_2_out);
  and and_1 (and_1_out, xor_3_out, xor_1_out);
  xor xor_4 (xor_4_out, X[7], Output[7]);
  Multiplexer #(.select(3), .enable("false")) multiplexer_1 (
    .in0(not_1_out), .in1(not_1_out), .in2(and_2_out), .in3(and_1_out), .in4(not_1_out), .in5(not_1_out),
    .in6(not_1_out), .in7(not_1_out), .out(OF), .sel(op_code));
  and and_2 (and_2_out, not_2_out, xor_4_out);
endmodule

module CF (
  input  [2:0] op_code,
  input  Adder,
  input  Subtractor,
  output out_4
);

  wire not_1_out;

  not not_1 (not_1_out, 1'b1);
  Multiplexer #(.select(3), .enable("false")) multiplexer_1 (
    .in0(not_1_out), .in1(not_1_out), .in2(Adder), .in3(Subtractor), .in4(not_1_out), .in5(not_1_out),
    .in6(not_1_out), .in7(not_1_out), .out(out_4), .sel(op_code));
endmodule

module test (
  input  [2:0] op_code,
  input  [7:0] X,
  input  [7:0] Y,
  output [7:0] Result,
  output SF,
  output ZF,
  output CF,
  output OF,
  output EQ
);

  AllTogether alltogether_1 (
    .op_code(op_code), .X(X), .Y(Y), .SF(SF), .ZF(ZF), .CF(CF), .OF(OF), .EQ(EQ), .Result(Result));
endmodule
