// Logisim project part1.circ as structural Verilog: 5 circuits, main circuit main
module main (
);


  // Notes on the sheet:
  //   cs31 lab3, part 1
  //   Zakir Hossain, Neel Gupta
endmodule

module signext2to4 (
  input  [1:0] _2_bit_input,
  output [3:0] _4_bit_output
);


  assign _4_bit_output = {{3{_2_bit_input[1]}}, _2_bit_input[0]};

  // Notes on the sheet:
  //   01 -> 0001
  //   00-> 0000
  //   10-> 1110
  //   11-> 1111
endmodule

module fulladder (
  input  X,
  input  Y,
  input  Carry_in,
  output Sum,
  output C_out
);

  wire and_1_out, and_2_out, xor_1_out;

  xor xor_1 (xor_1_out, X, Y);
  and and_1 (and_1_out, X, Y);
  and and_2 (and_2_out, xor_1_out, Carry_in);
  xor xor_2 (Sum, xor_1_out, Carry_in);
  or or_1 (C_out, and_2_out, and_1_out);
endmodule

module fulladder4 (
  input  [3:0] Input_1,
  input  [3:0] Input_2,
  input  Carry_in,
  output [3:0] Sum,
  output Carry_out
);

  wire fulladder_1_c_out, fulladder_2_c_out, fulladder_3_c_out;

  fulladder fulladder_1 (.X(Input_1[0]), .Y(Input_2[3]), .Carry_in(Carry_in), .Sum(Sum[0]), .C_out(fulladder_1_c_out));
  fulladder fulladder_2 (
    .X(Input_1[1]), .Y(Input_2[2]), .Carry_in(fulladder_1_c_out), .Sum(Sum[1]), .C_out(fulladder_2_c_out));
  fulladder fulladder_3 (
    .X(Input_1[2]), .Y(Input_2[1]), .Carry_in(fulladder_2_c_out), .Sum(Sum[2]), .C_out(fulladder_3_c_out));
  fulladder fulladder_4 (.X(Input_1[3]), .Y(Input_2[0]), .Carry_in(fulladder_3_c_out), .Sum(Sum[3]), .C_out(Carry_out));
endmodule

module PuttingAllTogether (
  input  [3:0] X,
  input  [1:0] y,
  input  carry_in,
  output [3:0] Sum,
  output Carry_out
);

  wire [3:0] signext2to4__4_bit_output;

  signext2to4 signext2to4 (._2_bit_input(y), ._4_bit_output(signext2to4__4_bit_output));
  fulladder4 fulladder4 (
    .Input_1(X), .Input_2(signext2to4__4_bit_output), .Carry_in(carry_in), .Sum(Sum), .Carry_out(Carry_out));
endmodule
